// Logisim project onetimepad.circ as structural Verilog: 1 circuit, main circuit main
module main (
);

  wire and_1_out, and_2_out, and_3_out, and_4_out, clock_1_out, d_ff_1_q, j_k_ff_1_qn, keyboard_1_avail,
       not_1_out, not_2_out, not_3_out, or_1_out, or_2_out;
  wire [6:0] keyboard_1_data;
  wire [7:0] bit_extender_1_out, counter_1_q, ram_1_dout, random_1_out, xor_8_out;

  Random #(.seed(2357)) random_1 (.next(1'b1), .clk(and_1_out), .out(random_1_out));  // open: clr
  Clock clock_1 (.out(clock_1_out));
  Keyboard #(.buflen(100)) keyboard_1 (
    .clk(clock_1_out), .avail(keyboard_1_avail), .data(keyboard_1_data));  // open: re, clr
  xor xor_1 (xor_8_out[7], random_1_out[7], ram_1_dout[7]);
  xor xor_2 (xor_8_out[6], random_1_out[6], ram_1_dout[6]);
  xor xor_3 (xor_8_out[5], random_1_out[5], ram_1_dout[5]);
  xor xor_4 (xor_8_out[4], random_1_out[4], ram_1_dout[4]);
  xor xor_5 (xor_8_out[3], random_1_out[3], ram_1_dout[3]);
  xor xor_6 (xor_8_out[2], random_1_out[2], ram_1_dout[2]);
  xor xor_7 (xor_8_out[1], random_1_out[1], ram_1_dout[1]);
  xor xor_8 (xor_8_out[0], random_1_out[0], ram_1_dout[0]);
  Counter counter_1 (.clr(and_2_out), .clk(and_3_out), .Q(counter_1_q));  // open: load, up, count, D, carry
  and and_1 (and_1_out, clock_1_out, not_2_out);
  not not_1 (not_1_out, 1'b1);
  J_K_Flip_Flop j_k_ff_1 (.J(1'b1), .K(not_1_out), .clk(and_1_out), .Qn(j_k_ff_1_qn));  // open: Q, preset, reset
  and and_2 (and_2_out, j_k_ff_1_qn, and_1_out);
  and and_3 (and_3_out, clock_1_out, or_1_out);
  not not_2 (not_2_out, keyboard_1_avail);
  D_Flip_Flop d_ff_1 (.D(1'b1), .clk(and_1_out), .Q(d_ff_1_q));  // open: Qn, preset, reset
  not not_3 (not_3_out, j_k_ff_1_qn);
  RAM ram_1 (
    .addr(counter_1_q), .we(j_k_ff_1_qn), .oe(d_ff_1_q), .clk(clock_1_out), .din(bit_extender_1_out),
    .dout(ram_1_dout));
  and and_4 (and_4_out, not_3_out, or_1_out);
  RAM ram_2 (.addr(counter_1_q), .we(and_4_out), .oe(1'b1), .clk(and_1_out), .din(xor_8_out));  // open: dout
  assign bit_extender_1_out = {{1{1'b0}}, keyboard_1_data};  // Bit_Extender bit_extender_1
  or or_1 (or_1_out, or_2_out, j_k_ff_1_qn);
  or or_2 (or_2_out, ram_1_dout[0], ram_1_dout[1], ram_1_dout[2], ram_1_dout[3], ram_1_dout[4], ram_1_dout[5], ram_1_dout[6], ram_1_dout[7]);

  // Notes on the sheet:
  //   CHARACTERS
  //   PSEUDO NUMBER GENERATOR
  //   KEY
  //   INPUT KEYBOARD
  //   RESET CNT
  //   COUNTER
  //   ENABLE OUTPUT
  //   ------------> INPUT BUFFER(PLAINTEXT)
  //   ----------->CIPHER MEMORY
endmodule
